// Logisim project Proiect_Final.circ as structural Verilog: 8 circuits, main circuit main
module main (
  output [7:0] out_1,
  output [7:0] out_2,
  output [7:0] out_3
);

  wire I2, I3, I4, I5, I6, I7, I8, I9, I10, I11, sageata_1_out_3, XOR1, XOR2, XOR3, XOR4, XOR5, XOR6, XOR7,
       XOR8, XOR9, XOR10;
  wire [1:0] kepresser_1_out_12;
  wire [2:0] button_3_out, keyboard_1__4_6_0, keyboard_1_out_8, keyboard_1_out_10, keyboard_1_out_12;
  wire [3:0] keyboard_1__0_3_0, keyboard_1_out_7, keyboard_1_out_9, keyboard_1_out_11, PUNCT;
  wire [4:0] _0_out, _5_out, B_out, button_4_out, button_5_out, button_7_out, ent_out, G_out, P_out, T_out;
  wire [10:0] buttonpresser_1_out_8, buttonpresser_2_out_8, buttonpresser_3_out_8, buttonpresser_4_out_8,
       buttonpresser_5_out_8, buttonpresser_6_out_8, buttonpresser_7_out_8, buttonpresser_8_out_8,
       buttonpresser_9_out_8, buttonpresser_10_out_8, kepresser_1_out_11, kepresser_2_out_11,
       multiplexer_1_out;
  wire [21:0] multiplexer_2_out, sageata_1_out_2;

  xor xor_1 (XOR1, 1'b1, I2);
  xor xor_2 (XOR6, I6, I7);
  Button _2 (.out(_5_out[3]));
  Button _3 (.out(_5_out[2]));
  Button _1 (.out(_5_out[4]));
  buttonpresser buttonpresser_1 (
    .in_7(_5_out), .in_6(1'b1), .in_2(11'h494), .in_3(11'h498), .in_4(11'h47a), .in_5(11'h458),
    .in_1(11'h4ba), .out_8(buttonpresser_1_out_8), .out_9(I2));
  Button E (.out(T_out[2]));
  Button Q (.out(T_out[4]));
  Button W (.out(T_out[3]));
  buttonpresser buttonpresser_2 (
    .in_7(T_out), .in_6(I5), .in_2(11'h4b6), .in_3(11'h492), .in_4(11'h476), .in_5(11'h454), .in_1(11'h4b0),
    .out_8(buttonpresser_2_out_8), .out_9(I6));
  Button S (.out(G_out[3]));
  Button A (.out(G_out[4]));
  Button D (.out(G_out[2]));
  buttonpresser buttonpresser_3 (
    .in_7(G_out), .in_6(I6), .in_2(11'h4ae), .in_3(11'h48c), .in_4(11'h46e), .in_5(11'h470), .in_1(11'h4d0),
    .out_8(buttonpresser_3_out_8), .out_9(I7));
  Button X (.out(B_out[3]));
  Button C (.out(B_out[2]));
  Button Z (.out(B_out[4]));
  buttonpresser buttonpresser_4 (
    .in_7(B_out), .in_6(I8), .in_2(11'h4a8), .in_3(11'h486), .in_4(11'h48a), .in_5(11'h468), .in_1(11'h4c8),
    .out_8(buttonpresser_4_out_8), .out_9(I9));
  xor xor_3 (XOR2, I2, I3);
  xor xor_4 (XOR7, I7, I8);
  Button _5 (.out(_5_out[0]));
  Button _4 (.out(_5_out[1]));
  Button Y (.out(P_out[4]));
  Button R (.out(T_out[1]));
  Button T (.out(T_out[0]));
  Button G (.out(G_out[0]));
  Button F (.out(G_out[1]));
  Button B (.out(B_out[0]));
  Button N (.out(button_5_out[4]));
  Button V (.out(B_out[1]));
  xor xor_5 (XOR3, I3, I4);
  xor xor_6 (XOR8, I8, I9);
  Button _8 (.out(_0_out[2]));
  Button _7 (.out(_0_out[3]));
  Button _6 (.out(_0_out[4]));
  buttonpresser buttonpresser_5 (
    .in_7(_0_out), .in_6(I2), .in_2(11'h518), .in_3(11'h4f8), .in_4(11'h4f4), .in_5(11'h4da), .in_1(11'h514),
    .out_8(buttonpresser_5_out_8), .out_9(I3));
  Button U (.out(P_out[3]));
  Button I (.out(P_out[2]));
  buttonpresser buttonpresser_6 (
    .in_7(P_out), .in_6(I4), .in_2(11'h512), .in_3(11'h50c), .in_4(11'h4f2), .in_5(11'h4d6), .in_1(11'h536),
    .out_8(buttonpresser_6_out_8), .out_9(I5));
  Button H (.out(button_4_out[4]));
  Button J (.out(button_4_out[3]));
  Button K (.out(button_4_out[2]));
  buttonpresser buttonpresser_7 (
    .in_7(button_4_out), .in_6(I7), .in_2(11'h52e), .in_3(11'h50a), .in_4(11'h4ec), .in_5(11'h4ce),
    .in_1(11'h530), .out_8(buttonpresser_7_out_8), .out_9(I8));
  Button button (.out(button_5_out[2]));
  Button M (.out(button_5_out[3]));
  buttonpresser buttonpresser_8 (
    .in_7(button_5_out), .in_6(I9), .in_2(11'h524), .in_3(11'h506), .in_4(11'h4ea), .in_5(11'h4c4),
    .in_1(11'h528), .out_8(buttonpresser_8_out_8), .out_9(I10));
  xor xor_7 (XOR4, I4, I5);
  xor xor_8 (XOR9, I9, I10);
  Button _9 (.out(_0_out[1]));
  Button _0 (.out(_0_out[0]));
  Button O (.out(P_out[1]));
  Button P (.out(P_out[0]));
  Button button_2 (.out(button_7_out[4]));
  Button button_3 (.out(button_3_out[0]));
  Button L (.out(button_4_out[1]));
  Button button_4 (.out(button_4_out[0]));
  Button button_5 (.out(button_5_out[0]));
  Button button_6 (.out(button_5_out[1]));
  xor xor_9 (XOR5, I5, I6);
  xor xor_10 (XOR10, I10, I11);
  Button button_7 (.out(button_7_out[0]));
  Button button_8 (.out(button_7_out[1]));
  Button button_9 (.out(button_7_out[2]));
  Button button_10 (.out(button_7_out[3]));
  buttonpresser buttonpresser_9 (
    .in_7(button_7_out), .in_6(I3), .in_2(11'h53a), .in_3(11'h574), .in_4(11'h56c), .in_5(11'h550),
    .in_1(11'h556), .out_8(buttonpresser_9_out_8), .out_9(I4));
  Button SPACE (.out(button_3_out[2]));
  Button BCK (.out(button_3_out[1]));
  buttonpresser buttonpresser_10 (
    .in_7({2'b00, button_3_out}), .in_6(I10), .in_2(11'h598), .in_3(11'h4a4), .in_1(11'h548),
    .out_8(buttonpresser_10_out_8), .out_9(I11));  // open: in_4, in_5
  Button up (.out(ent_out[4]));
  Button left (.out(ent_out[1]));
  Button down (.out(ent_out[2]));
  Button right (.out(ent_out[3]));
  sageata sageata_1 (.in_1(ent_out), .out_3(sageata_1_out_3), .out_2(sageata_1_out_2));
  kepresser kepresser_1 (
    .in_1(buttonpresser_1_out_8), .in_2(buttonpresser_5_out_8), .in_3(buttonpresser_9_out_8),
    .in_4(buttonpresser_6_out_8), .in_5(buttonpresser_2_out_8), .in_6(XOR1), .in_7(XOR2), .in_8(XOR3),
    .in_9(XOR4), .in_10(XOR5), .out_11(kepresser_1_out_11), .out_12(kepresser_1_out_12[0]));
  kepresser kepresser_2 (
    .in_1(buttonpresser_3_out_8), .in_2(buttonpresser_7_out_8), .in_3(buttonpresser_4_out_8),
    .in_4(buttonpresser_8_out_8), .in_5(buttonpresser_10_out_8), .in_6(XOR6), .in_7(XOR7), .in_8(XOR8),
    .in_9(XOR9), .in_10(XOR10), .out_11(kepresser_2_out_11), .out_12(kepresser_1_out_12[1]));
  Button ent (.out(ent_out[0]));
  Multiplexer #(.select(2), .width(11)) multiplexer_1 (
    .in0({11{1'b0}}), .in1(kepresser_1_out_11), .in2(kepresser_2_out_11), .in3({11{1'b0}}),
    .out(multiplexer_1_out), .sel(kepresser_1_out_12), .en(1'b1));
  Multiplexer #(.width(22)) multiplexer_2 (
    .in0({{11{1'b0}}, multiplexer_1_out}), .in1(sageata_1_out_2), .out(multiplexer_2_out),
    .sel(sageata_1_out_3), .en(1'b1));
  keyboard keyboard_1 (
    ._0_3_0(keyboard_1__0_3_0), ._4_6_0(keyboard_1__4_6_0), .out_7(keyboard_1_out_7),
    .out_8(keyboard_1_out_8), .out_9(keyboard_1_out_9), .out_11(keyboard_1_out_11),
    .out_10(keyboard_1_out_10), .out_12(keyboard_1_out_12), .in_1(multiplexer_2_out), .out_2(out_2),
    .out_4(PUNCT), .out_3(out_3));
  _7_Segment_Display u_7_segment_display_1 (
    .g(keyboard_1__0_3_0[3]), .f(keyboard_1__0_3_0[2]), .a(keyboard_1__0_3_0[1]), .b(keyboard_1__0_3_0[0]),
    .e(keyboard_1__4_6_0[0]), .d(keyboard_1__4_6_0[1]), .c(keyboard_1__4_6_0[2]), .dp(PUNCT[0]));
  _7_Segment_Display u_7_segment_display_2 (
    .g(keyboard_1_out_7[3]), .f(keyboard_1_out_7[2]), .a(keyboard_1_out_7[1]), .b(keyboard_1_out_7[0]),
    .e(keyboard_1_out_8[0]), .d(keyboard_1_out_8[1]), .c(keyboard_1_out_8[2]), .dp(PUNCT[1]));
  _7_Segment_Display u_7_segment_display_3 (
    .g(keyboard_1_out_9[3]), .f(keyboard_1_out_9[2]), .a(keyboard_1_out_9[1]), .b(keyboard_1_out_9[0]),
    .e(keyboard_1_out_10[0]), .d(keyboard_1_out_10[1]), .c(keyboard_1_out_10[2]), .dp(PUNCT[2]));
  _7_Segment_Display u_7_segment_display_4 (
    .g(keyboard_1_out_11[3]), .f(keyboard_1_out_11[2]), .a(keyboard_1_out_11[1]), .b(keyboard_1_out_11[0]),
    .e(keyboard_1_out_12[0]), .d(keyboard_1_out_12[1]), .c(keyboard_1_out_12[2]), .dp(PUNCT[3]));
endmodule

module buttonpresser (
  input  [10:0] in_1,
  input  [10:0] in_2,
  input  [10:0] in_3,
  input  [10:0] in_4,
  input  [10:0] in_5,
  input  in_6,
  input  [4:0] in_7,
  output [10:0] out_8,
  output out_9
);

  wire nor_1_out, or_1_out;

  Multiplexer #(.select(5), .width(11)) multiplexer_1 (
    .in0({11{1'b0}}), .in1(in_1), .in2(in_2), .in4(in_3), .in8(in_4), .in16(in_5), .out(out_8), .sel(in_7),
    .en(1'b1));  // open: in3, in5, in6, in7, in9, in10, in11, in12, in13, in14, in15, in17, in18, in19, in20, in21, in22, in23, in24, in25, in26, in27, in28, in29, in30, in31
  and and_1 (out_9, in_6, nor_1_out);
  nor nor_1 (nor_1_out, in_7[0], in_7[1], in_7[2], in_7[3], in_7[4]);
  or or_1 (or_1_out, out_8[1], out_8[2], out_8[3], out_8[4], out_8[5], out_8[6], out_8[7], out_8[8]);
endmodule

module kepresser (
  input  [10:0] in_1,
  input  [10:0] in_2,
  input  [10:0] in_3,
  input  [10:0] in_4,
  input  [10:0] in_5,
  input  in_6,
  input  in_7,
  input  in_8,
  input  in_9,
  input  in_10,
  output [10:0] out_11,
  output out_12
);

  Multiplexer #(.select(5), .width(11)) multiplexer_1 (
    .in0({11{1'b0}}), .in1(in_1), .in2(in_2), .in4(in_3), .in8(in_4), .in16(in_5), .out(out_11),
    .sel({in_10, in_9, in_8, in_7, in_6}), .en(1'b1));  // open: in3, in5, in6, in7, in9, in10, in11, in12, in13, in14, in15, in17, in18, in19, in20, in21, in22, in23, in24, in25, in26, in27, in28, in29, in30, in31
  or or_1 (out_12, in_6, in_7, in_8, in_9, in_10);
  // NOR_Gate nor_1 has open pins: in0=out_11[1], in1=out_11[2], in2=out_11[3], in3=out_11[4], in4=out_11[5], in5=out_11[6], in6=out_11[7], in7=out_11[8], out=open
endmodule

module keyboard (
  input  [21:0] in_1,
  output [7:0] out_2,
  output [7:0] out_3,
  output [3:0] out_4,
  output [3:0] _0_3_0,
  output [2:0] _4_6_0,
  output [3:0] out_7,
  output [2:0] out_8,
  output [3:0] out_9,
  output [2:0] out_10,
  output [3:0] out_11,
  output [2:0] out_12
);

  wire and_3_out, and_4_out, and_5_out, and_6_out, and_7_out, and_8_out, BCK, clock_1_out, E0_Check_p2,
       ENTER, ENTER_CHECK_p2, not_1_out, not_2_out, not_3_out, not_5_out, not_6_out, NOT_E0, or_1_out,
       TRANSFORMARE_p3, TRANSFORMARE_p4, TRANSFORMARE_SPECIALA_p3, TRANSFORMARE_SPECIALA_p4;
  wire [1:0] POZ;
  wire [3:0] counter_1_q;
  wire [6:0] afisare_1_p6, afisare_1_p7, afisare_1_p8, afisare_1_p9;
  wire [7:7] bit_extender_1_out, bit_extender_2_out, bit_extender_3_out, bit_extender_4_out;

  Counter #(.width(4), .max('ha)) counter_1 (.Q(counter_1_q), .clk(clock_1_out));  // open: load, D, count, carry, clr
  Clock clock_1 (.out(clock_1_out));
  not not_1 (not_1_out, counter_1_q[2]);
  // Enter_Check ENTER_CHECK: pin names not known; wires that end beside it: in_1[9:2], ENTER_CHECK_p2, counter_1_q[1]
  // Verificare_BackSpace BackSpace_Check: pin names not known; wires that end beside it: in_1[9:2], BCK
  // E0_Check E0_Check: pin names not known; wires that end beside it: in_1[20:13], E0_Check_p2
  not not_2 (not_2_out, BCK);
  not not_3 (not_3_out, E0_Check_p2);
  not not_4 (NOT_E0, E0_Check_p2);
  not not_5 (not_5_out, counter_1_q[0]);
  // AND_Gate and_1 has open pins: in0=not_5_out, in1=counter_1_q[1], in2=not_1_out, in3=counter_1_q[3], out=open
  and and_2 (ENTER, ENTER_CHECK_p2, 1'b1);
  and and_3 (and_3_out, not_2_out, not_3_out);
  // Transformare TRANSFORMARE: pin names not known; wires that end beside it: in_1[9:2], and_3_out, TRANSFORMARE_p3, TRANSFORMARE_p4
  not not_6 (not_6_out, TRANSFORMARE_p4);
  or or_1 (or_1_out, BCK, not_6_out);
  and and_4 (and_4_out, 1'b1, NOT_E0);
  // Transformare_Speciala TRANSFORMARE_SPECIALA: pin names not known; wires that end beside it: in_1[9:2], E0_Check_p2, TRANSFORMARE_SPECIALA_p3, TRANSFORMARE_SPECIALA_p4
  and and_5 (and_5_out, E0_Check_p2, 1'b1);
  and and_6 (and_6_out, or_1_out, and_4_out);
  and and_7 (and_7_out, TRANSFORMARE_SPECIALA_p4, E0_Check_p2);
  and and_8 (and_8_out, and_5_out, clock_1_out);
  Counter #(.width(2), .max('h3)) counter_2 (
    .load(TRANSFORMARE_SPECIALA_p3), .count(and_7_out), .Q(POZ), .clk(and_8_out), .clr(ENTER));  // open: D, carry
  // PUNCT PUNCT: pin names not known; wires that end beside it: POZ, out_4
  // Afisare afisare_1: pin names not known; wires that end beside it: ENTER, TRANSFORMARE_p3, {BCK, POZ}, and_6_out, clock_1_out, afisare_1_p6, afisare_1_p7, afisare_1_p8, afisare_1_p9
  assign {bit_extender_1_out[7], _0_3_0[1:0], _4_6_0, _0_3_0[2], _0_3_0[3]} = {{1{1'b0}}, afisare_1_p6};  // Bit_Extender bit_extender_1
  assign {bit_extender_2_out[7], out_7[1:0], out_8, out_7[2], out_7[3]} = {{1{1'b0}}, afisare_1_p7};  // Bit_Extender bit_extender_2
  assign {bit_extender_3_out[7], out_9[1:0], out_10, out_9[2], out_9[3]} = {{1{1'b0}}, afisare_1_p8};  // Bit_Extender bit_extender_3
  assign {bit_extender_4_out[7], out_11[1:0], out_12, out_11[2], out_11[3]} = {{1{1'b0}}, afisare_1_p9};  // Bit_Extender bit_extender_4
  _7_Segment_Display u_7_segment_display_1 (
    .g(_0_3_0[3]), .f(_0_3_0[2]), .a(_0_3_0[1]), .b(_0_3_0[0]), .e(_4_6_0[0]), .d(_4_6_0[1]), .c(_4_6_0[2]),
    .dp(out_4[0]));
  _7_Segment_Display u_7_segment_display_2 (
    .g(out_7[3]), .f(out_7[2]), .a(out_7[1]), .b(out_7[0]), .e(out_8[0]), .d(out_8[1]), .c(out_8[2]),
    .dp(out_4[1]));
  _7_Segment_Display u_7_segment_display_3 (
    .g(out_9[3]), .f(out_9[2]), .a(out_9[1]), .b(out_9[0]), .e(out_10[0]), .d(out_10[1]), .c(out_10[2]),
    .dp(out_4[2]));
  _7_Segment_Display u_7_segment_display_4 (
    .g(out_11[3]), .f(out_11[2]), .a(out_11[1]), .b(out_11[0]), .e(out_12[0]), .d(out_12[1]), .c(out_12[2]),
    .dp(out_4[3]));

  assign out_2 = in_1[9:2];
  assign out_3 = in_1[20:13];

  // Other names for the same wires on the sheet: _0_3_1[3:0] = out_7; _0_3_2[3:0] = out_9; _0_3_3[3:0] = out_11;
  //   _4_6_1[2:0] = out_8; _4_6_2[2:0] = out_10; _4_6_3[2:0] = out_12; DATA[7:0] = in_1[9:2];
  //   DATA2[7:0] = in_1[20:13]; PUNCT[3:0] = out_4
endmodule

module zerocheck (
  input  [10:0] in_1,
  output out_2
);

  wire not_1_out, not_2_out, not_3_out, not_4_out, not_5_out, not_6_out, not_7_out, not_8_out, not_9_out,
       not_10_out, not_11_out;

  and and_1 (out_2, not_1_out, not_2_out, not_3_out, not_4_out, not_5_out, not_6_out, not_7_out, not_8_out, not_9_out, not_10_out, not_11_out);
  not not_1 (not_1_out, in_1[0]);
  not not_2 (not_2_out, in_1[1]);
  not not_3 (not_3_out, in_1[2]);
  not not_4 (not_4_out, in_1[3]);
  not not_5 (not_5_out, in_1[4]);
  not not_6 (not_6_out, in_1[5]);
  not not_7 (not_7_out, in_1[6]);
  not not_8 (not_8_out, in_1[7]);
  not not_9 (not_9_out, in_1[8]);
  not not_10 (not_10_out, in_1[9]);
  not not_11 (not_11_out, in_1[10]);
endmodule

module sageata (
  input  [4:0] in_1,
  output [21:0] out_2,
  output out_3
);

  Multiplexer #(.select(5), .width(22)) multiplexer_1 (
    .in1(22'h96a), .in2(22'h3c09ac), .in4(22'h3c09ca), .in8(22'h3c09d2), .in16(22'h3c09d4), .out(out_2),
    .sel(in_1));  // open: in0, in3, in5, in6, in7, in9, in10, in11, in12, in13, in14, in15, in17, in18, in19, in20, in21, in22, in23, in24, in25, in26, in27, in28, in29, in30, in31, en
  or or_1 (out_3, in_1[0], in_1[1], in_1[2], in_1[3], in_1[4]);
endmodule

module _55 (
  input  in_1,
  output out_2
);

  wire not_1_out, not_2_out, not_3_out, not_4_out;
  wire [7:0] counter_1_q;

  Counter #(.max('h39)) counter_1 (
    .load(1'b0), .count(1'b1), .Q(counter_1_q), .clk(in_1), .clr(1'b0));  // open: D, carry
  not not_1 (not_1_out, counter_1_q[1]);
  not not_2 (not_2_out, counter_1_q[2]);
  not not_3 (not_3_out, counter_1_q[6]);
  not not_4 (not_4_out, counter_1_q[7]);
  and and_1 (out_2, counter_1_q[0], not_1_out, not_2_out, counter_1_q[3], counter_1_q[4], counter_1_q[5], not_3_out, not_4_out);
endmodule

module verif1 (
  input  [7:0] in_1,
  input  [7:0] in_2,
  output out_3
);

  wire xnor_1_out, xnor_2_out, xnor_3_out, xnor_4_out, xnor_5_out, xnor_6_out, xnor_7_out, xnor_8_out;

  xnor xnor_1 (xnor_1_out, in_1[0], in_2[0]);
  xnor xnor_2 (xnor_2_out, in_1[1], in_2[1]);
  xnor xnor_3 (xnor_3_out, in_1[2], in_2[2]);
  xnor xnor_4 (xnor_4_out, in_1[3], in_2[3]);
  xnor xnor_5 (xnor_5_out, in_1[4], in_2[4]);
  xnor xnor_6 (xnor_6_out, in_1[5], in_2[5]);
  xnor xnor_7 (xnor_7_out, in_1[6], in_2[6]);
  xnor xnor_8 (xnor_8_out, in_1[7], in_2[7]);
  and and_1 (out_3, xnor_1_out, xnor_2_out, xnor_3_out, xnor_4_out, xnor_5_out, xnor_6_out, xnor_7_out, xnor_8_out);
endmodule
